// Logisim project 2024.circ as structural Verilog: 5 circuits, main circuit main
module main (
);

  wire clk;
  wire [3:0] _1b, _2b, _3b, _4b, _5b, _6b, _7b, _8b, _9b, _10b, _11b, _12b, _13b, _14b, _15b, _16b;
  wire [6:0] key;
  wire [11:0] decoder_1_out1, decoder_2_out1, decoder_3_out1, decoder_4_out1, decoder_5_out1, decoder_6_out1,
       decoder_7_out1, decoder_8_out1, decoder_9_out1, decoder_10_out1, decoder_11_out1, decoder_12_out1,
       decoder_13_out1, decoder_14_out1, decoder_15_out1, decoder_16_out1;
  wire [15:0] _00, _01, _02, _03, _10, _11, _12, _13, _20, _21, _22, _23, _30, _31, _32, _33;

  Clock clock_1 (.out(clk));
  Hex_Digit_Display hex_digit_display_1 (.value(_00[11:8]));  // open: dp
  Hex_Digit_Display hex_digit_display_2 (.value(_00[15:12]));  // open: dp
  Hex_Digit_Display hex_digit_display_3 (.value(_10[11:8]));  // open: dp
  Hex_Digit_Display hex_digit_display_4 (.value(_10[15:12]));  // open: dp
  Hex_Digit_Display hex_digit_display_5 (.value(_20[15:12]));  // open: dp
  Hex_Digit_Display hex_digit_display_6 (.value(_20[11:8]));  // open: dp
  Hex_Digit_Display hex_digit_display_7 (.value(_30[11:8]));  // open: dp
  Hex_Digit_Display hex_digit_display_8 (.value(_30[15:12]));  // open: dp
  Register #(.width(4)) register_1 (.Q(_1b));  // open: D, en, clk, clr
  Register #(.width(4)) register_2 (.Q(_5b));  // open: D, en, clk, clr
  Register #(.width(4)) register_3 (.Q(_9b));  // open: D, en, clk, clr
  Register #(.width(4)) register_4 (.Q(_13b));  // open: D, en, clk, clr
  Hex_Digit_Display hex_digit_display_9 (.value(_00[7:4]));  // open: dp
  Hex_Digit_Display hex_digit_display_10 (.value(_00[3:0]));  // open: dp
  Hex_Digit_Display hex_digit_display_11 (.value(_10[7:4]));  // open: dp
  Hex_Digit_Display hex_digit_display_12 (.value(_10[3:0]));  // open: dp
  Hex_Digit_Display hex_digit_display_13 (.value(_20[3:0]));  // open: dp
  Hex_Digit_Display hex_digit_display_14 (.value(_20[7:4]));  // open: dp
  Hex_Digit_Display hex_digit_display_15 (.value(_30[3:0]));  // open: dp
  Hex_Digit_Display hex_digit_display_16 (.value(_30[7:4]));  // open: dp
  Register #(.width(4)) register_5 (.Q(_2b));  // open: D, en, clk, clr
  Register #(.width(4)) register_6 (.Q(_6b));  // open: D, en, clk, clr
  Register #(.width(4)) register_7 (.Q(_10b));  // open: D, en, clk, clr
  Register #(.width(4)) register_8 (.Q(_14b));  // open: D, en, clk, clr
  Hex_Digit_Display hex_digit_display_17 (.value(_01[15:12]));  // open: dp
  Hex_Digit_Display hex_digit_display_18 (.value(_11[15:12]));  // open: dp
  Hex_Digit_Display hex_digit_display_19 (.value(_21[15:12]));  // open: dp
  Hex_Digit_Display hex_digit_display_20 (.value(_31[15:12]));  // open: dp
  Register #(.width(4)) register_9 (.Q(_3b));  // open: D, en, clk, clr
  Register #(.width(4)) register_10 (.Q(_7b));  // open: D, en, clk, clr
  Register #(.width(4)) register_11 (.Q(_11b));  // open: D, en, clk, clr
  Register #(.width(4)) register_12 (.Q(_15b));  // open: D, en, clk, clr
  Hex_Digit_Display hex_digit_display_21 (.value(_01[11:8]));  // open: dp
  Hex_Digit_Display hex_digit_display_22 (.value(_01[7:4]));  // open: dp
  Hex_Digit_Display hex_digit_display_23 (.value(_11[7:4]));  // open: dp
  Hex_Digit_Display hex_digit_display_24 (.value(_11[11:8]));  // open: dp
  Hex_Digit_Display hex_digit_display_25 (.value(_21[11:8]));  // open: dp
  Hex_Digit_Display hex_digit_display_26 (.value(_21[7:4]));  // open: dp
  Hex_Digit_Display hex_digit_display_27 (.value(_31[7:4]));  // open: dp
  Hex_Digit_Display hex_digit_display_28 (.value(_31[11:8]));  // open: dp
  Keyboard keyboard_1 (.clk(clk), .data(key));  // open: re, clr, avail
  Register #(.width(4)) register_13 (.Q(_4b));  // open: D, en, clk, clr
  Register #(.width(4)) register_14 (.Q(_8b));  // open: D, en, clk, clr
  Register #(.width(4)) register_15 (.Q(_12b));  // open: D, en, clk, clr
  Register #(.width(4)) register_16 (.Q(_16b));  // open: D, en, clk, clr
  Hex_Digit_Display hex_digit_display_29 (.value(_01[3:0]));  // open: dp
  Hex_Digit_Display hex_digit_display_30 (.value(_11[3:0]));  // open: dp
  Hex_Digit_Display hex_digit_display_31 (.value(_21[3:0]));  // open: dp
  Hex_Digit_Display hex_digit_display_32 (.value(_31[3:0]));  // open: dp
  Hex_Digit_Display hex_digit_display_33 (.value(_02[15:12]));  // open: dp
  Hex_Digit_Display hex_digit_display_34 (.value(_02[11:8]));  // open: dp
  Hex_Digit_Display hex_digit_display_35 (.value(_12[15:12]));  // open: dp
  Hex_Digit_Display hex_digit_display_36 (.value(_12[11:8]));  // open: dp
  Hex_Digit_Display hex_digit_display_37 (.value(_22[11:8]));  // open: dp
  Hex_Digit_Display hex_digit_display_38 (.value(_22[15:12]));  // open: dp
  Hex_Digit_Display hex_digit_display_39 (.value(_32[15:12]));  // open: dp
  Hex_Digit_Display hex_digit_display_40 (.value(_32[11:8]));  // open: dp
  Hex_Digit_Display hex_digit_display_41 (.value(_02[3:0]));  // open: dp
  Hex_Digit_Display hex_digit_display_42 (.value(_02[7:4]));  // open: dp
  Hex_Digit_Display hex_digit_display_43 (.value(_12[7:4]));  // open: dp
  Hex_Digit_Display hex_digit_display_44 (.value(_12[3:0]));  // open: dp
  Hex_Digit_Display hex_digit_display_45 (.value(_22[3:0]));  // open: dp
  Hex_Digit_Display hex_digit_display_46 (.value(_22[7:4]));  // open: dp
  Hex_Digit_Display hex_digit_display_47 (.value(_32[7:4]));  // open: dp
  Hex_Digit_Display hex_digit_display_48 (.value(_32[3:0]));  // open: dp
  Hex_Digit_Display hex_digit_display_49 (.value(_03[15:12]));  // open: dp
  Hex_Digit_Display hex_digit_display_50 (.value(_13[15:12]));  // open: dp
  Hex_Digit_Display hex_digit_display_51 (.value(_23[15:12]));  // open: dp
  Hex_Digit_Display hex_digit_display_52 (.value(_33[15:12]));  // open: dp
  Hex_Digit_Display hex_digit_display_53 (.value(_03[11:8]));  // open: dp
  Hex_Digit_Display hex_digit_display_54 (.value(_03[7:4]));  // open: dp
  Hex_Digit_Display hex_digit_display_55 (.value(_13[7:4]));  // open: dp
  Hex_Digit_Display hex_digit_display_56 (.value(_13[11:8]));  // open: dp
  Hex_Digit_Display hex_digit_display_57 (.value(_23[7:4]));  // open: dp
  Hex_Digit_Display hex_digit_display_58 (.value(_23[11:8]));  // open: dp
  Hex_Digit_Display hex_digit_display_59 (.value(_33[11:8]));  // open: dp
  Hex_Digit_Display hex_digit_display_60 (.value(_33[7:4]));  // open: dp
  Hex_Digit_Display hex_digit_display_61 (.value(_03[3:0]));  // open: dp
  Hex_Digit_Display hex_digit_display_62 (.value(_13[3:0]));  // open: dp
  Hex_Digit_Display hex_digit_display_63 (.value(_23[3:0]));  // open: dp
  Hex_Digit_Display hex_digit_display_64 (.value(_33[3:0]));  // open: dp
  brody_bot brody_bot_1 (.clk(clk));  // open: _1st, _2nd, _3rd, _4th, _1st_2, _2nd_2, _3rd_2, _4th_2
  brody_bot brody_bot_2 (.clk(clk));  // open: _1st, _2nd, _3rd, _4th, _1st_2, _2nd_2, _3rd_2, _4th_2
  brody_bot brody_bot_3 (.clk(clk));  // open: _1st, _2nd, _3rd, _4th, _1st_2, _2nd_2, _3rd_2, _4th_2
  brody_bot brody_bot_4 (.clk(clk));  // open: _1st, _2nd, _3rd, _4th, _1st_2, _2nd_2, _3rd_2, _4th_2
  Decoder #(.select(4), .disabled(0), .enable("false")) decoder_1 (
    .out1(decoder_1_out1[0]), .out2(decoder_1_out1[1]), .out3(decoder_1_out1[2]), .out4(decoder_1_out1[3]),
    .out5(decoder_1_out1[4]), .out6(decoder_1_out1[5]), .out7(decoder_1_out1[6]), .out8(decoder_1_out1[7]),
    .out9(decoder_1_out1[8]), .out10(decoder_1_out1[9]), .out11(decoder_1_out1[10]),
    .out12(decoder_1_out1[11]), .sel(_1b));  // open: out0, out13, out14, out15
  Decoder #(.select(4), .disabled(0), .enable("false")) decoder_2 (
    .out1(decoder_2_out1[0]), .out2(decoder_2_out1[1]), .out3(decoder_2_out1[2]), .out4(decoder_2_out1[3]),
    .out5(decoder_2_out1[4]), .out6(decoder_2_out1[5]), .out7(decoder_2_out1[6]), .out8(decoder_2_out1[7]),
    .out9(decoder_2_out1[8]), .out10(decoder_2_out1[9]), .out11(decoder_2_out1[10]),
    .out12(decoder_2_out1[11]), .sel(_5b));  // open: out0, out13, out14, out15
  Decoder #(.select(4), .disabled(0), .enable("false")) decoder_3 (
    .out1(decoder_3_out1[0]), .out2(decoder_3_out1[1]), .out3(decoder_3_out1[2]), .out4(decoder_3_out1[3]),
    .out5(decoder_3_out1[4]), .out6(decoder_3_out1[5]), .out7(decoder_3_out1[6]), .out8(decoder_3_out1[7]),
    .out9(decoder_3_out1[8]), .out10(decoder_3_out1[9]), .out11(decoder_3_out1[10]),
    .out12(decoder_3_out1[11]), .sel(_9b));  // open: out0, out13, out14, out15
  Decoder #(.select(4), .disabled(0), .enable("false")) decoder_4 (
    .out1(decoder_4_out1[0]), .out2(decoder_4_out1[1]), .out3(decoder_4_out1[2]), .out4(decoder_4_out1[3]),
    .out5(decoder_4_out1[4]), .out6(decoder_4_out1[5]), .out7(decoder_4_out1[6]), .out8(decoder_4_out1[7]),
    .out9(decoder_4_out1[8]), .out10(decoder_4_out1[9]), .out11(decoder_4_out1[10]),
    .out12(decoder_4_out1[11]), .sel(_13b));  // open: out0, out13, out14, out15
  Decoder #(.select(4), .disabled(0), .enable("false")) decoder_5 (
    .out1(decoder_5_out1[0]), .out2(decoder_5_out1[1]), .out3(decoder_5_out1[2]), .out4(decoder_5_out1[3]),
    .out5(decoder_5_out1[4]), .out6(decoder_5_out1[5]), .out7(decoder_5_out1[6]), .out8(decoder_5_out1[7]),
    .out9(decoder_5_out1[8]), .out10(decoder_5_out1[9]), .out11(decoder_5_out1[10]),
    .out12(decoder_5_out1[11]), .sel(_2b));  // open: out0, out13, out14, out15
  bcd bcd_1 (._12bit_Input(decoder_1_out1), .BCD_Output(_00));
  Decoder #(.select(4), .disabled(0), .enable("false")) decoder_6 (
    .out1(decoder_6_out1[0]), .out2(decoder_6_out1[1]), .out3(decoder_6_out1[2]), .out4(decoder_6_out1[3]),
    .out5(decoder_6_out1[4]), .out6(decoder_6_out1[5]), .out7(decoder_6_out1[6]), .out8(decoder_6_out1[7]),
    .out9(decoder_6_out1[8]), .out10(decoder_6_out1[9]), .out11(decoder_6_out1[10]),
    .out12(decoder_6_out1[11]), .sel(_6b));  // open: out0, out13, out14, out15
  bcd bcd_2 (._12bit_Input(decoder_2_out1), .BCD_Output(_10));
  Decoder #(.select(4), .disabled(0), .enable("false")) decoder_7 (
    .out1(decoder_7_out1[0]), .out2(decoder_7_out1[1]), .out3(decoder_7_out1[2]), .out4(decoder_7_out1[3]),
    .out5(decoder_7_out1[4]), .out6(decoder_7_out1[5]), .out7(decoder_7_out1[6]), .out8(decoder_7_out1[7]),
    .out9(decoder_7_out1[8]), .out10(decoder_7_out1[9]), .out11(decoder_7_out1[10]),
    .out12(decoder_7_out1[11]), .sel(_10b));  // open: out0, out13, out14, out15
  bcd bcd_3 (._12bit_Input(decoder_3_out1), .BCD_Output(_20));
  Decoder #(.select(4), .disabled(0), .enable("false")) decoder_8 (
    .out1(decoder_8_out1[0]), .out2(decoder_8_out1[1]), .out3(decoder_8_out1[2]), .out4(decoder_8_out1[3]),
    .out5(decoder_8_out1[4]), .out6(decoder_8_out1[5]), .out7(decoder_8_out1[6]), .out8(decoder_8_out1[7]),
    .out9(decoder_8_out1[8]), .out10(decoder_8_out1[9]), .out11(decoder_8_out1[10]),
    .out12(decoder_8_out1[11]), .sel(_14b));  // open: out0, out13, out14, out15
  bcd bcd_4 (._12bit_Input(decoder_4_out1), .BCD_Output(_30));
  bcd bcd_5 (._12bit_Input(decoder_5_out1), .BCD_Output(_01));
  bcd bcd_6 (._12bit_Input(decoder_6_out1), .BCD_Output(_11));
  bcd bcd_7 (._12bit_Input(decoder_7_out1), .BCD_Output(_21));
  bcd bcd_8 (._12bit_Input(decoder_8_out1), .BCD_Output(_31));
  Decoder #(.select(4), .disabled(0), .enable("false")) decoder_9 (
    .out1(decoder_9_out1[0]), .out2(decoder_9_out1[1]), .out3(decoder_9_out1[2]), .out4(decoder_9_out1[3]),
    .out5(decoder_9_out1[4]), .out6(decoder_9_out1[5]), .out7(decoder_9_out1[6]), .out8(decoder_9_out1[7]),
    .out9(decoder_9_out1[8]), .out10(decoder_9_out1[9]), .out11(decoder_9_out1[10]),
    .out12(decoder_9_out1[11]), .sel(_3b));  // open: out0, out13, out14, out15
  Decoder #(.select(4), .disabled(0), .enable("false")) decoder_10 (
    .out1(decoder_10_out1[0]), .out2(decoder_10_out1[1]), .out3(decoder_10_out1[2]),
    .out4(decoder_10_out1[3]), .out5(decoder_10_out1[4]), .out6(decoder_10_out1[5]),
    .out7(decoder_10_out1[6]), .out8(decoder_10_out1[7]), .out9(decoder_10_out1[8]),
    .out10(decoder_10_out1[9]), .out11(decoder_10_out1[10]), .out12(decoder_10_out1[11]), .sel(_7b));  // open: out0, out13, out14, out15
  Decoder #(.select(4), .disabled(0), .enable("false")) decoder_11 (
    .out1(decoder_11_out1[0]), .out2(decoder_11_out1[1]), .out3(decoder_11_out1[2]),
    .out4(decoder_11_out1[3]), .out5(decoder_11_out1[4]), .out6(decoder_11_out1[5]),
    .out7(decoder_11_out1[6]), .out8(decoder_11_out1[7]), .out9(decoder_11_out1[8]),
    .out10(decoder_11_out1[9]), .out11(decoder_11_out1[10]), .out12(decoder_11_out1[11]), .sel(_11b));  // open: out0, out13, out14, out15
  Decoder #(.select(4), .disabled(0), .enable("false")) decoder_12 (
    .out1(decoder_12_out1[0]), .out2(decoder_12_out1[1]), .out3(decoder_12_out1[2]),
    .out4(decoder_12_out1[3]), .out5(decoder_12_out1[4]), .out6(decoder_12_out1[5]),
    .out7(decoder_12_out1[6]), .out8(decoder_12_out1[7]), .out9(decoder_12_out1[8]),
    .out10(decoder_12_out1[9]), .out11(decoder_12_out1[10]), .out12(decoder_12_out1[11]), .sel(_15b));  // open: out0, out13, out14, out15
  Decoder #(.select(4), .disabled(0), .enable("false")) decoder_13 (
    .out1(decoder_13_out1[0]), .out2(decoder_13_out1[1]), .out3(decoder_13_out1[2]),
    .out4(decoder_13_out1[3]), .out5(decoder_13_out1[4]), .out6(decoder_13_out1[5]),
    .out7(decoder_13_out1[6]), .out8(decoder_13_out1[7]), .out9(decoder_13_out1[8]),
    .out10(decoder_13_out1[9]), .out11(decoder_13_out1[10]), .out12(decoder_13_out1[11]), .sel(_4b));  // open: out0, out13, out14, out15
  bcd bcd_9 (._12bit_Input(decoder_9_out1), .BCD_Output(_02));
  Decoder #(.select(4), .disabled(0), .enable("false")) decoder_14 (
    .out1(decoder_14_out1[0]), .out2(decoder_14_out1[1]), .out3(decoder_14_out1[2]),
    .out4(decoder_14_out1[3]), .out5(decoder_14_out1[4]), .out6(decoder_14_out1[5]),
    .out7(decoder_14_out1[6]), .out8(decoder_14_out1[7]), .out9(decoder_14_out1[8]),
    .out10(decoder_14_out1[9]), .out11(decoder_14_out1[10]), .out12(decoder_14_out1[11]), .sel(_8b));  // open: out0, out13, out14, out15
  bcd bcd_10 (._12bit_Input(decoder_10_out1), .BCD_Output(_12));
  Decoder #(.select(4), .disabled(0), .enable("false")) decoder_15 (
    .out1(decoder_15_out1[0]), .out2(decoder_15_out1[1]), .out3(decoder_15_out1[2]),
    .out4(decoder_15_out1[3]), .out5(decoder_15_out1[4]), .out6(decoder_15_out1[5]),
    .out7(decoder_15_out1[6]), .out8(decoder_15_out1[7]), .out9(decoder_15_out1[8]),
    .out10(decoder_15_out1[9]), .out11(decoder_15_out1[10]), .out12(decoder_15_out1[11]), .sel(_12b));  // open: out0, out13, out14, out15
  bcd bcd_11 (._12bit_Input(decoder_11_out1), .BCD_Output(_22));
  Decoder #(.select(4), .disabled(0), .enable("false")) decoder_16 (
    .out1(decoder_16_out1[0]), .out2(decoder_16_out1[1]), .out3(decoder_16_out1[2]),
    .out4(decoder_16_out1[3]), .out5(decoder_16_out1[4]), .out6(decoder_16_out1[5]),
    .out7(decoder_16_out1[6]), .out8(decoder_16_out1[7]), .out9(decoder_16_out1[8]),
    .out10(decoder_16_out1[9]), .out11(decoder_16_out1[10]), .out12(decoder_16_out1[11]), .sel(_16b));  // open: out0, out13, out14, out15
  bcd bcd_12 (._12bit_Input(decoder_12_out1), .BCD_Output(_32));
  bcd bcd_13 (._12bit_Input(decoder_13_out1), .BCD_Output(_03));
  bcd bcd_14 (._12bit_Input(decoder_14_out1), .BCD_Output(_13));
  bcd bcd_15 (._12bit_Input(decoder_15_out1), .BCD_Output(_23));
  bcd bcd_16 (._12bit_Input(decoder_16_out1), .BCD_Output(_33));
endmodule

module bcd_helper (
  input  [3:0] inp,
  output [3:0] out
);

  wire comparator_1_eq, comparator_1_lt, or_1_out;
  wire [3:0] adder_1_out;

  // Probe on inp
  Adder #(.width(4)) adder_1 (.a(4'b0011), .b(inp), .out(adder_1_out));  // open: cin, cout
  Comparator #(.width(4), .mode("unsigned")) comparator_1 (
    .a(4'b0101), .b(inp), .eq(comparator_1_eq), .lt(comparator_1_lt));  // open: gt
  or or_1 (or_1_out, comparator_1_eq, comparator_1_lt);
  Multiplexer #(.width(4)) multiplexer_1 (.in0(inp), .in1(adder_1_out), .out(out), .sel(or_1_out));  // open: en
endmodule

module bcd (
  input  [11:0] _12bit_Input,
  output [15:0] BCD_Output
);

  wire [2:0] bcd_helper_12_out, bcd_helper_15_out;
  wire [3:0] bcd_helper_1_out, bcd_helper_2_out, bcd_helper_3_out, bcd_helper_4_out, bcd_helper_5_out,
       bcd_helper_6_out, bcd_helper_7_out, bcd_helper_8_out, bcd_helper_9_out, bcd_helper_10_out,
       bcd_helper_11_out, bcd_helper_13_out, bcd_helper_14_out;

  // Probe on _12bit_Input
  bcd_helper bcd_helper_1 (.inp({1'b0, _12bit_Input[11:9]}), .out(bcd_helper_1_out));
  bcd_helper bcd_helper_2 (.inp({bcd_helper_1_out[2:0], _12bit_Input[8]}), .out(bcd_helper_2_out));
  bcd_helper bcd_helper_3 (.inp({bcd_helper_2_out[2:0], _12bit_Input[7]}), .out(bcd_helper_3_out));
  bcd_helper bcd_helper_4 (.inp({bcd_helper_3_out[2:0], _12bit_Input[6]}), .out(bcd_helper_4_out));
  bcd_helper bcd_helper_5 (
    .inp({1'b0, bcd_helper_1_out[3], bcd_helper_2_out[3], bcd_helper_3_out[3]}), .out(bcd_helper_5_out));
  bcd_helper bcd_helper_6 (.inp({bcd_helper_4_out[2:0], _12bit_Input[5]}), .out(bcd_helper_6_out));
  bcd_helper bcd_helper_7 (.inp({bcd_helper_5_out[2:0], bcd_helper_4_out[3]}), .out(bcd_helper_7_out));
  bcd_helper bcd_helper_8 (.inp({bcd_helper_6_out[2:0], _12bit_Input[4]}), .out(bcd_helper_8_out));
  bcd_helper bcd_helper_9 (.inp({bcd_helper_7_out[2:0], bcd_helper_6_out[3]}), .out(bcd_helper_9_out));
  bcd_helper bcd_helper_10 (.inp({bcd_helper_8_out[2:0], _12bit_Input[3]}), .out(bcd_helper_10_out));
  bcd_helper bcd_helper_11 (.inp({bcd_helper_9_out[2:0], bcd_helper_8_out[3]}), .out(bcd_helper_11_out));
  bcd_helper bcd_helper_12 (
    .inp({1'b0, bcd_helper_5_out[3], bcd_helper_7_out[3], bcd_helper_9_out[3]}),
    .out({BCD_Output[14], bcd_helper_12_out}));
  bcd_helper bcd_helper_13 (.inp({bcd_helper_10_out[2:0], _12bit_Input[2]}), .out(bcd_helper_13_out));
  bcd_helper bcd_helper_14 (.inp({bcd_helper_11_out[2:0], bcd_helper_10_out[3]}), .out(bcd_helper_14_out));
  bcd_helper bcd_helper_15 (.inp({bcd_helper_12_out, bcd_helper_11_out[3]}), .out({BCD_Output[13], bcd_helper_15_out}));
  bcd_helper bcd_helper_16 (.inp({bcd_helper_13_out[2:0], _12bit_Input[1]}), .out(BCD_Output[4:1]));
  bcd_helper bcd_helper_17 (.inp({bcd_helper_14_out[2:0], bcd_helper_13_out[3]}), .out(BCD_Output[8:5]));
  bcd_helper bcd_helper_18 (.inp({bcd_helper_15_out, bcd_helper_14_out[3]}), .out(BCD_Output[12:9]));
  // Probe on {1'b0, BCD_Output[14:12]}
  // Probe on BCD_Output[11:8]
  // Probe on BCD_Output[7:4]
  // Probe on {BCD_Output[3:1], _12bit_Input[0]}

  assign {BCD_Output[15], BCD_Output[0]} = {1'b0, _12bit_Input[0]};

  // Notes on the sheet:
  //   The double dable algorithm
endmodule

module brody_bot (
  input  [3:0] _1st,
  input  [3:0] _2nd,
  input  [3:0] _3rd,
  input  [3:0] _4th,
  input  clk,
  output [3:0] _1st_2,
  output [3:0] _2nd_2,
  output [3:0] _3rd_2,
  output [3:0] _4th_2
);
endmodule

module random_randy (
  input  [3:0] in_1,
  input  [3:0] in_2,
  input  [3:0] in_3,
  input  [3:0] in_4,
  input  [3:0] in_5,
  input  [3:0] in_6,
  input  [3:0] in_7,
  input  [3:0] in_8,
  input  [3:0] in_9,
  input  [3:0] in_10,
  input  [3:0] in_11,
  input  clk,
  input  [3:0] in_13,
  input  [3:0] in_14,
  input  [3:0] in_15,
  input  [3:0] in_16,
  input  [3:0] in_17
);

  wire [3:0] counter_1_q;

  Counter #(.width(4), .max('hf)) counter_1 (.Q(counter_1_q), .clk(clk));  // open: load, D, count, carry, clr
  Decoder #(.select(4), .disabled(0), .enable("false")) decoder_1 (.sel(counter_1_q));  // open: out0, out1, out2, out3, out4, out5, out6, out7, out8, out9, out10, out11, out12, out13, out14, out15

  // Notes on the sheet:
  //   ...sorta random (not at all)
endmodule
